// Logisim project Project1Given.circ as structural Verilog: 4 circuits, main circuit main
module main (
  input  in_1,
  input  in_2,
  input  in_3,
  input  in_4,
  input  Five,
  output N,
  output E,
  output [3:0] out_8
);

  wire fiveseven_1_a, fiveseven_1_b, fiveseven_1_c, fiveseven_1_d, fiveseven_1_e, fiveseven_1_f,
       fiveseven_1_g;

  Compare compare_1 (.X0(1'b1), .X1(1'b0), .X2(1'b1), .Y0(1'b1), .Y1(1'b1), .Y2(1'b1), .N(N), .E(E));
  Gray gray_1 (.B0(1'b1), .B1(1'b0), .B2(1'b1), .B3(1'b1), .G0(out_8[0]), .G1(out_8[1]), .G2(out_8[2]), .G3(out_8[3]));
  FiveSeven fiveseven_1 (
    .V(in_1), .W(in_2), .X(in_3), .Y(in_4), .Z(Five), .A(fiveseven_1_a), .B(fiveseven_1_b),
    .C(fiveseven_1_c), .D(fiveseven_1_d), .E(fiveseven_1_e), .F(fiveseven_1_f), .G(fiveseven_1_g));
  _7_Segment_Display u_7_segment_display_1 (
    .g(fiveseven_1_g), .f(fiveseven_1_f), .a(fiveseven_1_a), .b(fiveseven_1_b), .e(fiveseven_1_e),
    .d(fiveseven_1_d), .c(fiveseven_1_c));  // open: dp
endmodule

module Compare (
  input  X0,
  input  X1,
  input  X2,
  input  Y0,
  input  Y1,
  input  Y2,
  output N,
  output E
);

  wire and_1_out, and_2_out, and_3_out, and_4_out, and_6_out, and_7_out, not_1_out, not_2_out, not_3_out,
       xnor_1_out, xnor_2_out, xnor_3_out;

  not not_1 (not_1_out, X2);
  and and_1 (and_1_out, not_1_out, Y2);
  not not_2 (not_2_out, X1);
  not not_3 (not_3_out, X0);
  and and_2 (and_2_out, not_2_out, Y1);
  xnor xnor_1 (xnor_1_out, X0, Y0);
  xnor xnor_2 (xnor_2_out, X2, Y2);
  and and_3 (and_3_out, and_2_out, xnor_2_out);
  xnor xnor_3 (xnor_3_out, X1, Y1);
  and and_4 (and_4_out, not_3_out, Y0);
  and and_5 (E, xnor_1_out, xnor_3_out, xnor_2_out);
  and and_6 (and_6_out, xnor_2_out, xnor_3_out);
  and and_7 (and_7_out, and_4_out, and_6_out);
  or or_1 (N, and_1_out, and_3_out, and_7_out);
endmodule

module Gray (
  input  B0,
  input  B1,
  input  B2,
  input  B3,
  output G0,
  output G1,
  output G2,
  output G3
);

  wire and_1_out, and_2_out, and_3_out, and_4_out, and_5_out, and_6_out, and_7_out, not_1_out, not_2_out,
       not_3_out, not_4_out, not_5_out, not_6_out, not_7_out, or_1_out, or_2_out, or_3_out;

  not not_1 (not_1_out, B2);
  not not_2 (not_2_out, B0);
  not not_3 (not_3_out, B1);
  not not_4 (not_4_out, B3);
  not not_5 (not_5_out, B2);
  not not_6 (not_6_out, B0);
  not not_7 (not_7_out, B1);
  and and_1 (and_1_out, B0, B2);
  or or_1 (or_1_out, B0, B1);
  and and_2 (and_2_out, B0, B1);
  xor xor_1 (G3, and_1_out, B3);
  or or_2 (or_2_out, and_2_out, B2);
  and and_3 (and_3_out, B3, not_5_out);
  or or_3 (or_3_out, not_6_out, not_7_out);
  and and_4 (and_4_out, or_1_out, not_1_out);
  and and_5 (and_5_out, not_2_out, not_3_out, B2);
  and and_6 (and_6_out, or_2_out, not_4_out);
  and and_7 (and_7_out, and_3_out, or_3_out);
  not not_8 (G0, B1);
  or or_4 (G1, and_4_out, and_5_out);
  or or_5 (G2, and_6_out, and_7_out);

  // Notes on the sheet:
  //   B0B1
  //   B0B1B2
  //   B0+B1
  //   B3(~B2)
  //   (~B0)+(~B1)
  //   B3 XOR (B0B1B2)
  //   ~B2(B0+B1)
  //   B2(~B0)(~B1)
  //   B2+B0B1
  //   (~B3)(B2+B0B1)
  //   (B3(~B2))((~B0)+(~B1))
  //   G3=B3 XOR (B0B1B2)
  //   G0=~B1
  //   G1=(~B2(B0+B1))+(B2(~B0)(~B1))
  //   G2=((~B3)(B2+B0B1))+((B3(~B2)((~B0)+(~B1))
endmodule

module FiveSeven (
  input  V,
  input  W,
  input  X,
  input  Y,
  input  Z,
  output A,
  output B,
  output C,
  output D,
  output E,
  output F,
  output G
);
endmodule
